# Fritzing sketch CristalWood (saved by Fritzing 0.9.3b)
breadboards: 1

parts:
  Rev3 = Arduino Uno (Rev3)
  S2 = Momentary Switch [package=tactile_switch_smd]
  R1 = Resistor [tolerance=±5% resistance=220 package=THT]
  LED1 = RGB LED (com. cathode, rbg) [package="5 mm [THT]"]
  LED2 = RGB LED (com. cathode, rbg) [package="5 mm [THT]"]
  LED3 = RGB LED (com. cathode, rbg) [package="5 mm [THT]"]
  LED4 = RGB LED (com. cathode, rbg) [package="5 mm [THT]"]
  R2 = Resistor [tolerance=±5% resistance=220 package=THT]
  R3 = Resistor [tolerance=±5% resistance=220 package=THT]
  R4 = Resistor [tolerance=±5% resistance=220 package=THT]
  R5 = Resistor [tolerance=±5% resistance=220 package=THT]
  R6 = Resistor [tolerance=±5% resistance=220 package=THT]
  R7 = Resistor [tolerance=±5% resistance=220 package=THT]
  R8 = Resistor [tolerance=±5% resistance=220 package=THT]
  R9 = Resistor [tolerance=±5% resistance=220 package=THT]
  R10 = Resistor [tolerance=±5% resistance=220 package=THT]
  R11 = Resistor [tolerance=±5% resistance=220 package=THT]
  R12 = Resistor [tolerance=±5% resistance=220 package=THT]

nets:
  N1: Rev3.D9_PWM, R3.Pin_1, R6.Pin_1
  N2: Rev3.D10_PWM/SS, R1.Pin_1, R4.Pin_1
  N3: Rev3.D11_PWM/MOSI, R2.Pin_1, R5.Pin_1
  N4: Rev3.GND, S2.3, LED1.common_cathode, LED2.common_cathode, LED3.common_cathode, LED4.common_cathode
  N5: Rev3.D2, S2.1
  N6: Rev3.D3_PWM, R9.Pin_1, R12.Pin_1
  N7: Rev3.D5_PWM, R7.Pin_1, R10.Pin_1
  N8: Rev3.D6_PWM, R8.Pin_1, R11.Pin_1
  N9: R1.Pin_0, LED1.green_anode
  N10: LED1.red_anode, R3.Pin_0
  N11: LED1.blue_anode, R2.Pin_0
  N12: LED2.red_anode, R6.Pin_0
  N13: LED2.blue_anode, R5.Pin_0
  N14: LED2.green_anode, R4.Pin_0
  N15: LED3.red_anode, R9.Pin_0
  N16: LED3.blue_anode, R8.Pin_0
  N17: LED3.green_anode, R7.Pin_0
  N18: LED4.red_anode, R12.Pin_0
  N19: LED4.blue_anode, R11.Pin_0
  N20: LED4.green_anode, R10.Pin_0
